# Fritzing sketch capacitiveslider (saved by Fritzing 0.7.12b)
breadboards: 1

parts:
  Teensy1 = Teensy++ 2.0
  R1 = Resistor [tolerance=±5% resistance=10k package=THT]
  R2 = Resistor [tolerance=±5% resistance=10k package=THT]

nets:
  N1: Teensy1.F5, R2.Pin_0
  N2: Teensy1.F4, R1.Pin_0
  N3: Teensy1.VCC, R1.Pin_1, R2.Pin_1

notes:
  10k Resistor
